// Digital circuit CPU_main.dig as structural Verilog
module CPU_main (
  input  Acc_out,
  input  ALU_out,
  input  IR_out
);

  wire T1, T2, T3;
  wire [2:0] Counter_out;
  wire [7:0] Acc_q, alu_main_1_p5, IR_q, PC_out, W_BUS;

  CounterPreset PC (.en(T2), .in(W_BUS[0]), .out(PC_out[0]));  // open: C, dir, ld, clr, ovf
  assign W_BUS = T1 ? PC_out : 8'bz;  // Driver driver_1
  Register #(.Bits(8)) MAR (.D(W_BUS), .en(T1));  // open: C, Q
  Counter #(.Bits(3)) Counter (.out(Counter_out));  // open: en, C, clr, ovf
  // Probe on W_BUS
  ROM #(.AddrBits(8), .Bits(8)) ROM (.sel(T3), .D(W_BUS));  // open: A
  Decoder #(.Selector_Bits(3)) decoder_1 (
    .sel(Counter_out), .out_0(T1), .out_1(T2), .out_2(T3));  // open: out_3, out_4, out_5, out_6, out_7
  Register #(.Bits(8)) Acc (.Q(Acc_q));  // open: D, C, en
  assign W_BUS = Acc_out ? Acc_q : 8'bz;  // Driver driver_2
  Register #(.Bits(8)) IR (.D(W_BUS), .en(T3), .Q(IR_q));  // open: C
  // ALU_main alu_main_1: pin names not known; wires that end beside it: T1, T2, T3, W_BUS, alu_main_1_p5
  assign W_BUS = IR_out ? IR_q : 8'bz;  // Driver driver_3
  assign W_BUS = ALU_out ? alu_main_1_p5 : 8'bz;  // Driver driver_4
  Register #(.Bits(8)) B_reg (.D(W_BUS));  // open: C, en, Q
  Register #(.Bits(8)) Out_reg (.D(W_BUS));  // open: C, en, Q
  // Pins of 1 and 8 bits meet at W_BUS
  // Pins of 1 and 8 bits meet at PC_out
endmodule
